# Fritzing sketch EEPROM_Programmer_Breadboard_Schematic (saved by Fritzing 1.0.2b)
breadboards: 1

parts:
  ArduinoNano = Arduino Nano (Rev3.0)
  74HC595_1 = 74HC595 [package="DIP16 [THT]"]
  AT28C16 = IC, DIP package, 24 pins [chip_label=28C16]
  74HC595_2 = 74HC595 [package="DIP16 [THT]"]
  C2 = Ceramic Capacitor [capacitance=1nF voltage=35V package="100 mil [THT, multilayer]"]
  R4 = Resistor [tolerance=±5% power=0.25W resistance=10k package=THT]
  R5 = Resistor [tolerance=±5% power=0.25W resistance=680 package=THT]

nets:
  GND: ArduinoNano.GND, 74HC595_1.GND, 74HC595_1.OE, AT28C16.pin12, AT28C16.pin18, 74HC595_2.GND, 74HC595_2.OE
  N1: ArduinoNano.D2, 74HC595_1.SH_CP, 74HC595_2.SH_CP
  N2: ArduinoNano.D3, 74HC595_1.ST_CP, 74HC595_2.ST_CP
  N3: ArduinoNano.D4, 74HC595_1.DS
  N4: ArduinoNano.D5, AT28C16.pin17
  N5: ArduinoNano.D6, AT28C16.pin16
  N6: ArduinoNano.D7, AT28C16.pin15
  N7: ArduinoNano.D8, AT28C16.pin14
  N8: ArduinoNano.D9, AT28C16.pin13
  N9: ArduinoNano.D10, AT28C16.pin11
  N10: ArduinoNano.D11/MOSI, AT28C16.pin10
  N11: ArduinoNano.D12/MISO, AT28C16.pin9
  5V: ArduinoNano.5V, 74HC595_1.MR, 74HC595_1.VCC, AT28C16.pin24, 74HC595_2.MR, 74HC595_2.VCC, R4.Pin_0, R5.Pin_0
  N12: ArduinoNano.D13/SCK, C2.0, R4.Pin_1
  N13: 74HC595_1.Q5, AT28C16.pin19
  N14: 74HC595_1.Q6, AT28C16.pin22
  N15: 74HC595_1.Q7, AT28C16.pin23
  N16: 74HC595_1.Q7', 74HC595_2.DS
  N17: 74HC595_1.Q0, AT28C16.pin20
  N18: AT28C16.pin1, 74HC595_2.Q0
  N19: AT28C16.pin2, 74HC595_2.Q1
  N20: AT28C16.pin3, 74HC595_2.Q2
  N21: AT28C16.pin4, 74HC595_2.Q3
  N22: AT28C16.pin5, 74HC595_2.Q4
  N23: AT28C16.pin6, 74HC595_2.Q5
  N24: AT28C16.pin7, 74HC595_2.Q6
  N25: AT28C16.pin8, 74HC595_2.Q7
  N26: AT28C16.pin21, C2.1, R5.Pin_1
